# Fritzing sketch cricket (saved by Fritzing 0.9.10b)
breadboards: 1

parts:
  Mod1 = Amica NodeMCU DEVKIT 1.0
  RHT1 = Humidity and Temperature Sensor RHT03
  LED1 = LED - 5mm [color="Red (633nm)" current=0.030 package="5 mm [THT]"]
  R1 = Resistor [tolerance=±5% resistance=470 power=0.25 package="0402 [SMD]"]

nets:
  N1: Mod1.pin1, Mod1.pin_10, Mod1.pin_26, RHT1.Vcc
  N2: Mod1.pin2, Mod1.pin_9, Mod1.pin_25, Mod1.pin_29, RHT1.GND_2, R1.Pin_0
  N3: Mod1.pin_13, LED1.anode
  N4: Mod1.pin_14, RHT1.Data-signal
  N5: LED1.cathode, R1.Pin_1
